# Fritzing sketch metahack (saved by Fritzing 1.0.5)

parts:
  M1 = DOIT Esp32 DevKit v1 (30 pins long, 11 pins width) [part_number=ESP32S-PIN30]
  X1 = USB Connectors [package=usb-a-h]
  M2 = SN65HVD230 CAN Bus transciever module [package=THT]

nets:
  N1: M1.3V3, M2.pin_1
  GND: M1.GND, X1.GND, M2.pin_2
  N2: M1.D25, M2.pin_4
  N3: M1.D26, M2.pin_3
  N4: M1.VIN, X1.VBUS
  N5: X1.D-, M2.pin_6
  N6: X1.D+, M2.pin_5

custom parts:
  DOIT Esp32 DevKit v1 (30 pins long, 11 pins width): The DOIT Esp32 DevKit v1 is one of the development board created by DOIT to evaluate the ESP-WROOM-32 module. It is based on the ESP32 microcontroller that boasts Wifi, Bluetooth, Ethernet and Low Power support all in a single chip. (vanepp) made breadboard work, adjusted pin numbering and labels and reduced size of schematic and cleaned up pcb. This chip is 30pins long (2 x15) and 11 pins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
  SN65HVD230 CAN Bus transciever module: Bus Transceiver SN65HVD230 CAN Communication Module, for Arduino.
